# Fritzing sketch BrausteuerungV4 (saved by Fritzing 0.9.3b)
circuit board: 8.46667cm x 5.64444cm
breadboards: 1

parts:
  U2 = FS1000A - 433Mhz RF Transmitter [package=THT]
  Piezo1 = Piezo Speaker - PC Mount [part_number=COM-07950]  # not connected
  DS1 = DS18B20 1-Wire Temperature Sensor [part_number=DS18B20]
  VCC2 = Battery block 9V
  S2 = SWITCH-MOMENTARY-2 [package=tactile-switch-1101ne]
  R4 = Resistor [tolerance=±5% resistance=4.7k package=THT]
  R5 = Resistor [tolerance=±5% resistance=330 package=THT]
  LED2 = smd LED [color="Red (633nm)" package="1206 [SMD]"]
  D2 = Schottky Diode [part_number=1N5817 package="Melf DO-213 AB [SMD]"]
  R8 = Resistor [tolerance=±5% resistance=150k package=THT]
  R9 = Resistor [tolerance=±5% resistance=47k package=THT]
  S3 = Pushbutton [package="[THT]"]
  U3 = NodeMCU V1.0

nets:
  N1: U2.DATA, U3.D4
  VCC: U2.VCC, DS1.VDD, R4.Pin_1, U3.3V3
  GND: U2.GND, DS1.GND, VCC2.-, LED2.cathode, R9.Pin_0, S3.Pin_3, S3.Pin_4, U3.GND
  N2: DS1.DQ, R4.Pin_0, U3.D2
  N3: VCC2.+, S2.1
  N4: S2.2, D2.anode
  N5: R5.Pin_0, U3.D0
  N6: R5.Pin_1, LED2.anode
  N7: R8.Pin_0, R9.Pin_1, U3.A0
  N8: R8.Pin_1, U3.Vin
  N9: S3.Pin_1, S3.Pin_2, U3.D1

custom parts:
  FS1000A - 433Mhz RF Transmitter: This is 433Mhz RF transmitter with receiver kit for Arduino ARM MCU wireless Application environment: Remote control switch, receiver module, motorcycles, automobile anti-theft products, home security products, electric doors, shutter doors, windows, remote control socket, remote control LED, remote audio remote control electric doors, garage door remote control, remote control retractable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
  Piezo Speaker - PC Mount: This is a small 12mm round speaker that operates around the audible 2kHz range. You can use these speakers to create simple music or user interfaces. Each speaker is PTH solderable and requires an operating voltage of 3.5-5V with a mean current of 35mA max. These speakers also have a typical sound output of 95 dBA and a coil resistance of 42 ±6.3 ohms.
  NodeMCU V1.0: ESP8266 based NodeMCU
