# Fritzing sketch TX433MHz-Receiver-MX-RM-5V (saved by Fritzing 1.0.1rc)
breadboards: 1

parts:
  WeMos_D1_Mini1 = WeMos D1 Mini  # not connected
  U7 = RF-LINK_RX [package=rf-link_rx]
  R1 = Resistor [tolerance=±5% resistance=10k package="0805 [SMD]"]
  R2 = Resistor [tolerance=±5% resistance=220 package="0805 [SMD]"]

nets:
  N1: U7.GND, R2.Pin_1
  N2: U7.Data#2, R1.Pin_1
  N3: R1.Pin_0, R2.Pin_0

notes:
  MX-RM-5V
  Empfänger mit 17,5cm Stabantenne

custom parts:
  WeMos D1 Mini: The D1 mini is a mini wifi board based on ESP-8266EX.
  RF-LINK_RX: RF Link receivers- WRL-8947, 8948, 8949, 8950
